// Logisim project Bonus10.circ as structural Verilog: 1 circuit, main circuit main
module main (
  output s
);

  wire clock_1_out, d_ff_1_qn;

  Clock clock_1 (.out(clock_1_out));
  D_Flip_Flop d_ff_1 (.clk(clock_1_out), .D(d_ff_1_qn), .Q(s), .Qn(d_ff_1_qn));  // open: preset, en, reset
endmodule
