// Logisim project Bonus11.1.circ as structural Verilog: 1 circuit, main circuit main
module main (
  input  c
);

  wire A_q, and_1_out, and_2_out, and_3_out, and_4_out, and_5_out, and_6_out, and_7_out, and_8_out, B_q, C_q,
       D_q, E_q, h, or_1_out, or_2_out, or_3_out;

  Clock clock_1 (.out(h));
  and and_1 (and_1_out, ~c, E_q);  // AND_Gate
  and and_2 (and_2_out, D_q, ~c);  // AND_Gate
  and and_3 (and_3_out, B_q, ~c);  // AND_Gate
  and and_4 (and_4_out, E_q, c);
  D_Flip_Flop A (.clk(h), .D(and_1_out), .Q(A_q));  // open: Qn, preset, en, reset
  D_Flip_Flop E (.clk(h), .D(or_1_out), .Q(E_q));  // open: Qn, preset, en, reset
  or or_1 (or_1_out, and_2_out, and_3_out, and_4_out);
  and and_5 (and_5_out, C_q, c);
  or or_2 (or_2_out, and_5_out, A_q);
  D_Flip_Flop B (.clk(h), .D(or_2_out), .Q(B_q));  // open: Qn, preset, en, reset
  D_Flip_Flop u_C (.clk(h), .D(and_6_out), .Q(C_q));  // open: Qn, preset, en, reset
  and and_6 (and_6_out, c, B_q);
  and and_7 (and_7_out, C_q, ~c);  // AND_Gate
  and and_8 (and_8_out, c, D_q);
  D_Flip_Flop D (.clk(h), .D(or_3_out), .Q(D_q));  // open: Qn, preset, en, reset
  or or_3 (or_3_out, and_7_out, and_8_out);
endmodule
