// Logisim project Bonus11.2.circ as structural Verilog: 1 circuit, main circuit main
module main (
  output q0,
  output q1,
  output q2,
  output q3
);

  wire h_out, not_1_out;

  Clock h (.out(h_out));
  not not_1 (not_1_out, q3);
  D_Flip_Flop d_ff_1 (.clk(h_out), .D(not_1_out), .Q(q0));  // open: Qn, preset, en, reset
  D_Flip_Flop d_ff_2 (.clk(h_out), .D(q0), .Q(q1));  // open: Qn, preset, en, reset
  D_Flip_Flop d_ff_3 (.clk(h_out), .D(q1), .Q(q2));  // open: Qn, preset, en, reset
  D_Flip_Flop d_ff_4 (.clk(h_out), .D(q2), .Q(q3));  // open: Qn, preset, en, reset
endmodule
