// Logisim project Bonus12.circ as structural Verilog: 1 circuit, main circuit main
// h
module main (
  output s0,
  output s1,
  output s2
);

  wire and_1_out, clock_1_out, not_1_out;

  Clock clock_1 (.out(clock_1_out));
  and and_1 (and_1_out, ~s0, s1, s2);  // AND_Gate
  not not_1 (not_1_out, and_1_out);
  Counter #(.width(3), .max('h7)) counter_1 (
    .load(and_1_out), .D(3'b000), .count(not_1_out), .Q({s2, s1, s0}), .clk(clock_1_out));  // open: carry, clr
endmodule
