// Logisim project Bonus5.circ as structural Verilog: 1 circuit, main circuit main
module main (
  input  \config ,
  input  a1,
  input  a2,
  output b1,
  output b2
);

  wire not_1_out, not_2_out;

  assign b1 = \config  ? a1 : 1'bz;  // Controlled_Buffer controlled_buffer_1
  not not_1 (not_1_out, \config );
  assign b2 = not_1_out ? a1 : 1'bz;  // Controlled_Buffer controlled_buffer_2
  not not_2 (not_2_out, \config );
  assign b1 = not_2_out ? a2 : 1'bz;  // Controlled_Buffer controlled_buffer_3
  assign b2 = \config  ? a2 : 1'bz;  // Controlled_Buffer controlled_buffer_4
endmodule
