// Logisim project Bonus8.circ as structural Verilog: 1 circuit, main circuit main
module main (
  input  b0,
  input  e0,
  input  b1,
  input  e1,
  input  b2,
  input  e2,
  input  b3,
  input  e3,
  input  b4,
  input  e4,
  input  b5,
  input  e5,
  input  b6,
  input  e6,
  input  [2:0] ae,
  input  [1:0] as,
  input  b7,
  input  e7,
  input  [2:0] a,
  output s0,
  output s1,
  output s2,
  output s3,
  output s
);

  wire decoder_1_out0, decoder_1_out1, decoder_1_out2, decoder_1_out3, decoder_1_out4, decoder_1_out5,
       decoder_1_out6, decoder_1_out7, multiplexer_1_out;

  assign s = decoder_1_out0 ? b0 : 1'bz;  // Controlled_Buffer controlled_buffer_1
  assign s = decoder_1_out1 ? b1 : 1'bz;  // Controlled_Buffer controlled_buffer_2
  Decoder #(.select(3), .enable("false")) decoder_1 (
    .out0(decoder_1_out0), .out1(decoder_1_out1), .out2(decoder_1_out2), .out3(decoder_1_out3),
    .out4(decoder_1_out4), .out5(decoder_1_out5), .out6(decoder_1_out6), .out7(decoder_1_out7), .sel(a));
  assign s = decoder_1_out2 ? b2 : 1'bz;  // Controlled_Buffer controlled_buffer_3
  assign s = decoder_1_out3 ? b3 : 1'bz;  // Controlled_Buffer controlled_buffer_4
  assign s = decoder_1_out4 ? b4 : 1'bz;  // Controlled_Buffer controlled_buffer_5
  assign s = decoder_1_out5 ? b5 : 1'bz;  // Controlled_Buffer controlled_buffer_6
  assign s = decoder_1_out6 ? b6 : 1'bz;  // Controlled_Buffer controlled_buffer_7
  assign s = decoder_1_out7 ? b7 : 1'bz;  // Controlled_Buffer controlled_buffer_8
  Multiplexer #(.select(3), .enable("false")) multiplexer_1 (
    .in0(e0), .in1(e1), .in2(e2), .in3(e3), .in4(e4), .in5(e5), .in6(e6), .in7(e7), .out(multiplexer_1_out),
    .sel(ae));
  Decoder #(.select(2), .disabled(0)) decoder_2 (
    .out0(s0), .out1(s1), .out2(s2), .out3(s3), .sel(as), .en(multiplexer_1_out));
endmodule
