// Logisim project TD2-3.circ as structural Verilog: 1 circuit, main circuit main
module main (
  input  in_1,
  input  [3:0] X,
  input  [3:0] Y,
  input  in_4,
  output [3:0] out_5
);

  wire [3:0] multiplexer_1_out, multiplexer_2_out, shifter_1_out, shifter_2_out;

  Shifter #(.width(4)) shifter_1 (.in(X), .\dist (2'b01), .out(shifter_1_out));
  Shifter #(.width(4)) shifter_2 (.in(Y), .\dist (2'b01), .out(shifter_2_out));
  Multiplexer #(.width(4), .enable("false")) multiplexer_1 (
    .in0(Y), .in1(shifter_2_out), .out(multiplexer_1_out), .sel(in_4));
  Multiplexer #(.enable("false")) multiplexer_2 (
    .in0(X[0]), .in1(shifter_1_out[0]), .out(multiplexer_2_out[0]), .sel(in_1));
  Multiplexer #(.enable("false")) multiplexer_3 (
    .in0(X[1]), .in1(shifter_1_out[1]), .out(multiplexer_2_out[1]), .sel(in_1));
  Multiplexer #(.enable("false")) multiplexer_4 (
    .in0(X[2]), .in1(shifter_1_out[2]), .out(multiplexer_2_out[2]), .sel(in_1));
  Multiplexer #(.enable("false")) multiplexer_5 (
    .in0(X[3]), .in1(shifter_1_out[3]), .out(multiplexer_2_out[3]), .sel(in_1));
  Adder #(.width(4)) adder_1 (.a(multiplexer_2_out), .b(multiplexer_1_out), .out(out_5));  // open: cin, cout
endmodule
