// Logisim project TD2-4.circ as structural Verilog: 1 circuit, main circuit main
module main (
  input  a1,
  input  a0,
  input  X,
  input  Y,
  input  a0_2,
  input  a0_3,
  input  a1_2,
  input  a2,
  input  a3,
  input  v,
  input  v_2,
  input  a0_4,
  input  a1_3,
  output [15:0] out_14,
  output [1:0] out_15
);

  wire decoder_1_out3, decoder_2_out0, decoder_2_out1, decoder_2_out2, decoder_2_out3;
  wire [3:0] and_1_out, and_5_out;

  not not_1 (out_15[0], a0_2);
  and and_1 (and_1_out[0], ~a1_2, ~a0_3);  // AND_Gate
  and and_2 (and_1_out[1], ~a1_2, a0_3);  // AND_Gate
  and and_3 (and_1_out[2], a1_2, ~a0_3);  // AND_Gate
  and and_4 (and_1_out[3], a1_2, a0_3);
  // Probe on decoder_1_out3
  Decoder #(.select(2), .enable("false")) decoder_1 (.out3(decoder_1_out3), .sel({Y, X}));  // open: out0, out1, out2
  // Probe on and_1_out
  and and_5 (and_5_out[0], ~a1_3, ~a0_4, v_2);  // AND_Gate
  and and_6 (and_5_out[1], ~a1_3, a0_4, v_2);  // AND_Gate
  and and_7 (and_5_out[2], a1_3, ~a0_4, v_2);  // AND_Gate
  and and_8 (and_5_out[3], a1_3, a0_4, v_2);
  // Probe on and_5_out
  Decoder #(.select(2), .disabled(0)) decoder_2 (
    .out0(decoder_2_out0), .out1(decoder_2_out1), .out2(decoder_2_out2), .out3(decoder_2_out3),
    .sel({a3, a2}), .en(v));
  Decoder #(.select(2), .disabled(0)) decoder_3 (
    .out0(out_14[0]), .out1(out_14[1]), .out2(out_14[2]), .out3(out_14[3]), .sel({a1, a0}),
    .en(decoder_2_out0));
  Decoder #(.select(2), .disabled(0)) decoder_4 (
    .out0(out_14[4]), .out1(out_14[5]), .out2(out_14[6]), .out3(out_14[7]), .sel({a1, a0}),
    .en(decoder_2_out1));
  Decoder #(.select(2), .disabled(0)) decoder_5 (
    .out0(out_14[8]), .out1(out_14[9]), .out2(out_14[10]), .out3(out_14[11]), .sel({a1, a0}),
    .en(decoder_2_out2));
  Decoder #(.select(2), .disabled(0)) decoder_6 (
    .out0(out_14[12]), .out1(out_14[13]), .out2(out_14[14]), .out3(out_14[15]), .sel({a1, a0}),
    .en(decoder_2_out3));

  assign out_15[1] = a0_2;
endmodule
