// Logisim project TD2-5.circ as structural Verilog: 1 circuit, main circuit main
module main (
  input  a,
  input  v1,
  input  v0,
  input  a_2,
  input  v1_2,
  input  v0_2,
  input  v0_3,
  input  v1_3,
  input  v2,
  input  v3,
  input  v4,
  input  v5,
  input  v6,
  input  v7,
  input  [2:0] a_3,
  output s,
  output s_2,
  output s_3
);

  wire and_1_out, and_2_out, decoder_1_out0, decoder_1_out1, decoder_1_out2, decoder_1_out3, decoder_1_out4,
       decoder_1_out5, decoder_1_out6, decoder_1_out7, not_1_out;

  assign s_3 = decoder_1_out0 ? v0_3 : 1'bz;  // Controlled_Buffer controlled_buffer_1
  assign s_3 = decoder_1_out1 ? v1_3 : 1'bz;  // Controlled_Buffer controlled_buffer_2
  assign s_3 = decoder_1_out2 ? v2 : 1'bz;  // Controlled_Buffer controlled_buffer_3
  Decoder #(.select(3), .enable("false")) decoder_1 (
    .out0(decoder_1_out0), .out1(decoder_1_out1), .out2(decoder_1_out2), .out3(decoder_1_out3),
    .out4(decoder_1_out4), .out5(decoder_1_out5), .out6(decoder_1_out6), .out7(decoder_1_out7), .sel(a_3));
  and and_1 (and_1_out, ~a, v0);  // AND_Gate
  and and_2 (and_2_out, a, v1);
  assign s_3 = decoder_1_out3 ? v3 : 1'bz;  // Controlled_Buffer controlled_buffer_4
  assign s_3 = decoder_1_out4 ? v4 : 1'bz;  // Controlled_Buffer controlled_buffer_5
  assign s_3 = decoder_1_out5 ? v5 : 1'bz;  // Controlled_Buffer controlled_buffer_6
  assign s_3 = decoder_1_out6 ? v6 : 1'bz;  // Controlled_Buffer controlled_buffer_7
  or or_1 (s, and_1_out, and_2_out);
  assign s_3 = decoder_1_out7 ? v7 : 1'bz;  // Controlled_Buffer controlled_buffer_8
  not not_1 (not_1_out, a_2);
  assign s_2 = not_1_out ? v0_2 : 1'bz;  // Controlled_Buffer controlled_buffer_9
  assign s_2 = a_2 ? v1_2 : 1'bz;  // Controlled_Buffer controlled_buffer_10
endmodule
