// Logisim project TD3-1.circ as structural Verilog: 1 circuit, main circuit main
module main (
  input  R,
  input  S,
  input  J,
  input  K,
  input  D,
  input  D_2,
  input  T,
  output Q,
  output Q_2,
  output Q_3,
  output Q_4,
  output Q_5
);

  wire and_1_out, and_2_out, and_3_out, clock_1_out, not_1_out, or_1_out, or_2_out, xor_1_out;

  Clock clock_1 (.out(clock_1_out));
  and and_1 (and_1_out, R, ~Q);  // AND_Gate
  and and_2 (and_2_out, J, ~Q_2);  // AND_Gate
  and and_3 (and_3_out, ~K, Q_2);  // AND_Gate
  xor xor_1 (xor_1_out, D, Q_3);
  not not_1 (not_1_out, D_2);
  or or_1 (or_1_out, and_1_out, S);
  or or_2 (or_2_out, and_2_out, and_3_out);
  D_Flip_Flop d_ff_1 (.clk(clock_1_out), .D(or_1_out), .Q(Q));  // open: Qn, preset, en, reset
  D_Flip_Flop d_ff_2 (.clk(clock_1_out), .D(or_2_out), .Q(Q_2));  // open: Qn, preset, en, reset
  T_Flip_Flop t_ff_1 (.clk(clock_1_out), .T(xor_1_out), .Q(Q_3));  // open: Qn, preset, reset, en
  J_K_Flip_Flop j_k_ff_1 (.J(D_2), .clk(clock_1_out), .K(not_1_out), .Q(Q_4));  // open: Qn, preset, en, reset
  J_K_Flip_Flop j_k_ff_2 (.J(T), .clk(clock_1_out), .K(T), .Q(Q_5));  // open: Qn, preset, en, reset
endmodule
