// Logisim project TD3-3.circ as structural Verilog: 1 circuit, main circuit main
module main (
  input  e,
  output s0,
  output s1
);

  wire and_1_out, and_2_out, d_ff_1_q, h_out;

  Clock h (.out(h_out));
  D_Flip_Flop d_ff_1 (.clk(h_out), .D(e), .Q(d_ff_1_q));  // open: Qn, preset, en, reset
  and and_1 (and_1_out, e, ~d_ff_1_q);  // AND_Gate
  and and_2 (and_2_out, ~e, d_ff_1_q);  // AND_Gate
  D_Flip_Flop d_ff_2 (.clk(h_out), .D(and_1_out), .Q(s0));  // open: Qn, preset, en, reset
  D_Flip_Flop d_ff_3 (.clk(h_out), .D(and_2_out), .Q(s1));  // open: Qn, preset, en, reset
endmodule
