// Logisim project TD3-4-1.circ as structural Verilog: 2 circuits, main circuit main
module main (
  input  Nbre,
  input  Init,
  output Est_div
);

  wire D0_q, D1_q, D2_q, h_out, multiplexer_1_out, multiplexer_2_out, multiplexer_3_out, nor_1_out,
       reste_1_s0, reste_1_s1, reste_1_s2;

  reste reste_1 (.e0(D0_q), .e1(D1_q), .e2(D2_q), .b(Nbre), .s0(reste_1_s0), .s1(reste_1_s1), .s2(reste_1_s2));
  Clock h (.out(h_out));
  Multiplexer #(.enable("false")) multiplexer_1 (.in0(reste_1_s0), .in1(1'b0), .out(multiplexer_1_out), .sel(Init));
  Multiplexer #(.enable("false")) multiplexer_2 (.in0(reste_1_s1), .in1(1'b0), .out(multiplexer_2_out), .sel(Init));
  Multiplexer #(.enable("false")) multiplexer_3 (.in0(reste_1_s2), .in1(1'b0), .out(multiplexer_3_out), .sel(Init));
  D_Flip_Flop D0 (.clk(h_out), .D(multiplexer_1_out), .Q(D0_q));  // open: Qn, preset, en, reset
  D_Flip_Flop D1 (.clk(h_out), .D(multiplexer_2_out), .Q(D1_q));  // open: Qn, preset, en, reset
  D_Flip_Flop D2 (.clk(h_out), .D(multiplexer_3_out), .Q(D2_q));  // open: Qn, preset, en, reset
  nor nor_1 (nor_1_out, D0_q, D1_q, D2_q);
  D_Flip_Flop D0_2 (.clk(h_out), .D(nor_1_out), .Q(Est_div));  // open: Qn, preset, en, reset
endmodule

module reste (
  input  e0,
  input  e1,
  input  e2,
  input  b,
  output s0,
  output s1,
  output s2
);

  wire and_1_out, and_2_out, and_3_out, and_4_out, and_5_out, and_6_out, and_7_out, and_8_out;

  and and_1 (and_1_out, b, ~e2, ~e1);  // AND_Gate
  and and_2 (and_2_out, b, ~e2, e0);  // AND_Gate
  and and_3 (and_3_out, ~b, ~e2, e1, e0);  // AND_Gate
  and and_4 (and_4_out, ~b, e2, ~e1, ~e0);  // AND_Gate
  and and_5 (and_5_out, ~b, ~e2, ~e1, e0);  // AND_Gate
  and and_6 (and_6_out, ~b, e2, ~e1, ~e0);  // AND_Gate
  and and_7 (and_7_out, ~b, ~e2, e1, ~e0);  // AND_Gate
  and and_8 (and_8_out, b, e2, ~e1, ~e0);  // AND_Gate
  or or_1 (s0, and_1_out, and_3_out, and_4_out);
  or or_2 (s1, and_2_out, and_5_out, and_6_out);
  or or_3 (s2, and_7_out, and_8_out);
endmodule
