// Logisim project TD4-1.circ as structural Verilog: 1 circuit, main circuit main
module main (
);

  wire and_1_out, and_2_out, and_3_out, B_out, E1_q, E2_q, h_out, or_1_out;

  Button B (.out(B_out));
  Clock h (.out(h_out));
  D_Flip_Flop E2 (.clk(h_out), .D(B_out), .Q(E2_q));  // open: Qn, preset, en, reset
  D_Flip_Flop E1 (.clk(h_out), .D(or_1_out), .Q(E1_q));  // open: Qn, preset, en, reset
  and and_1 (and_1_out, B_out, ~E2_q, ~E1_q);  // AND_Gate
  and and_2 (and_2_out, E2_q, E1_q);
  and and_3 (and_3_out, ~B_out, E1_q);  // AND_Gate
  or or_1 (or_1_out, and_1_out, and_2_out, and_3_out);
  LED S (.in(E1_q));
endmodule
