// Logisim project TD4-4.circ as structural Verilog: 1 circuit, main circuit main
module main (
  input  C1,
  input  C0
);

  wire A, and_1_out, and_2_out, and_3_out, and_4_out, and_5_out, B, C, clock_1_out, D, or_1_out;
  wire [1:0] counter_1_q;

  and and_1 (and_1_out, ~C1, ~counter_1_q[1], counter_1_q[0]);  // AND_Gate
  and and_2 (and_2_out, ~C0, ~counter_1_q[1], ~counter_1_q[0]);  // AND_Gate
  and and_3 (and_3_out, C1, ~counter_1_q[1], counter_1_q[0]);  // AND_Gate
  and and_4 (and_4_out, counter_1_q[1], ~counter_1_q[0]);  // AND_Gate
  and and_5 (and_5_out, counter_1_q[1], counter_1_q[0]);
  or or_1 (or_1_out, and_2_out, and_3_out, and_4_out, and_5_out);
  Counter #(.width(2), .max('h3)) counter_1 (
    .load(and_1_out), .D(2'b11), .count(or_1_out), .Q(counter_1_q), .clk(clock_1_out));  // open: carry, clr
  Clock clock_1 (.out(clock_1_out));
  Decoder #(.select(2), .enable("false")) decoder_1 (.out0(A), .out1(B), .out2(C), .out3(D), .sel(counter_1_q));
  LED led_1 (.in(A));
  LED led_2 (.in(B));
  LED led_3 (.in(C));
  LED led_4 (.in(D));
endmodule
