// Logisim project TD5.circ as structural Verilog: 1 circuit, main circuit main
module main (
  input  Init,
  input  [7:0] n,
  output Res,
  output [7:0] S
);

  wire clock_1_out, doInit, doNext, isEnded, multiplexer_1_out, not_1_out, not_2_out, or_1_out, or_2_out;
  wire [1:0] Ei_q, rom_1_data_2;
  wire [2:0] rom_1_data;
  wire [7:0] adder_1_out, controlled_buffer_1_out, controlled_buffer_3_out, N0_q, N1_q, N_q, Q_q;

  not not_1 (not_1_out, Init);
  Register u_N (.D(n), .en(doInit), .Q(N_q), .clk(clock_1_out));  // open: clr
  Clock clock_1 (.out(clock_1_out));
  Multiplexer #(.select(3), .enable("false")) multiplexer_1 (
    .in0(Init), .in1(not_1_out), .in2(isEnded), .in6(1'b0), .in7(1'b1), .out(multiplexer_1_out),
    .sel(rom_1_data));  // open: in3, in4, in5
  not not_2 (not_2_out, multiplexer_1_out);
  Counter Q (.load(doInit), .D({8{1'b0}}), .count(doNext), .Q(Q_q), .clk(clock_1_out));  // open: carry, clr
  Counter #(.width(2), .max('h3)) Ei (
    .load(multiplexer_1_out), .D(rom_1_data_2), .count(not_2_out), .Q(Ei_q), .clk(clock_1_out));  // open: carry, clr
  assign controlled_buffer_1_out = doNext ? N1_q : 8'bz;  // Controlled_Buffer controlled_buffer_1
  or or_1 (or_1_out, doNext, doInit);
  assign controlled_buffer_1_out = doInit ? {8{1'b0}} : 8'bz;  // Controlled_Buffer controlled_buffer_2
  Comparator comparator_1 (.a(Q_q), .b(N_q), .eq(isEnded));  // open: gt, lt
  Register N0 (.D(controlled_buffer_1_out), .en(or_1_out), .Q(N0_q), .clk(clock_1_out));  // open: clr
  ROM #(.addrWidth(2)) rom_1 (.addr(Ei_q), .data({rom_1_data, rom_1_data_2, Res, doNext, doInit}), .sel(1'b1));
  Adder adder_1 (.a(N1_q), .b(N0_q), .out(adder_1_out));  // open: cin, cout
  assign controlled_buffer_3_out = doNext ? adder_1_out : 8'bz;  // Controlled_Buffer controlled_buffer_3
  or or_2 (or_2_out, doNext, doInit);
  assign controlled_buffer_3_out = doInit ? 8'h1 : 8'bz;  // Controlled_Buffer controlled_buffer_4
  Register N1 (.D(controlled_buffer_3_out), .en(or_2_out), .Q(N1_q), .clk(clock_1_out));  // open: clr
  assign S = Res ? N0_q : 8'bz;  // Controlled_Buffer controlled_buffer_5

  // Other names for the same wires on the sheet: doDisplay = Res

  // Notes on the sheet:
  //   contents of rom_1 (hex, n*v repeats v):
  //   21 58 ea 1c
endmodule
