// Logisim project bonus13.circ as structural Verilog: 1 circuit, main circuit main
module main (
  input  h,
  input  b,
  input  g,
  input  d,
  input  K,
  output H_2,
  output B_2,
  output G_2,
  output D_2
);

  wire and_1_out, and_2_out, and_3_out, e0_q, e1_q, h_out, or_1_out, or_2_out;

  and and_1 (and_1_out, g, ~e0_q, e1_q);  // AND_Gate
  and and_2 (and_2_out, ~e0_q, ~e1_q, K);  // AND_Gate
  and and_3 (and_3_out, d, h, e0_q, ~e1_q);  // AND_Gate
  or or_1 (or_1_out, and_3_out, and_1_out);
  or or_2 (or_2_out, and_1_out, and_2_out);
  Clock u_h (.out(h_out));
  D_Flip_Flop e1 (.clk(h_out), .D(or_1_out), .Q(e1_q));  // open: Qn, preset, en, reset
  D_Flip_Flop e0 (.clk(h_out), .D(or_2_out), .Q(e0_q));  // open: Qn, preset, en, reset
  and and_4 (H_2, ~h, e0_q, ~e1_q);  // AND_Gate
  and and_5 (B_2, ~b, e0_q, e1_q);  // AND_Gate
  and and_6 (G_2, ~g, ~e0_q, e1_q);  // AND_Gate
  and and_7 (D_2, ~d, e0_q, ~e1_q);  // AND_Gate
endmodule
